# Fritzing sketch esp8266-dht11 (saved by Fritzing 0.9.3b)
breadboards: 1

parts:
  U2 = NodeMCU V3.0
  DHT1 = DHT11 Humitidy and Temperature Sensor  # not connected
  R1 = Resistor [tolerance=±5% resistance=220 package=THT]

nets:
  N1: U2.D1, R1.Pin_1
  N2: U2.GND#6, U2.GND#13, U2.GND#16, U2.GND#33

custom parts:
  NodeMCU V3.0: ESP8266 based NodeMCU
  DHT11 Humitidy and Temperature Sensor: DHT11 Humidity and Temperature Sensor
